# Fritzing sketch Presse gel (saved by Fritzing 0.9.3b)

parts:
  Part1 = Arduino Nano (Rev3.0)
  J1 = Basic Servo
  M1 = fc-51 [package=THT]
  VCC1 = 4 x AAA Battery Mount

nets:
  GND: Part1.GND, J1.gnd, M1.pin2, VCC1.-
  N1: Part1.D2, M1.pin1
  N2: Part1.D3, J1.pulse
  5V: Part1.5V, J1.vcc, M1.pin3, VCC1.+

notes:
  Capteur de proximite
  Servomoteur a rotation continue
  arduino nano
  batterie ou power bank 5v
  Proximity sensor
  Continuously rotating servomotor
  battery or power bank 5v
  noir/black = -/ground
  rouge/red = +/vcc
  D2
  D3

// code stored in the sketch: code.ino
#include <Servo.h>

#define sensor 2

Servo servo;
/* Utilisation du capteur Ultrason HC-SR04 */

void setup() {
  servo.attach(3);
  pinMode(sensor,INPUT);
  Serial.begin(9600);
  servo.write(90);
  delay(500);
}

void loop() {
  // put your main code here, to run repeatedly:
  int value = digitalRead(sensor);
  servo.write(90);

  if (value == LOW )
  {
    servo.write(0);
    delay(5000);
    servo.write(180);
    delay(4500);
  }
}
